# Fritzing sketch SkyeTracker_ESP32 (saved by Fritzing 0.9.3b)
breadboards: 1

parts:
  R1 = Resistor [tolerance=±5% resistance=220 package=THT]
  R2 = Resistor [tolerance=±5% resistance=220 package=THT]
  Part1 = Real Time Clock Module - DS1307 RTC Breakout Board
  Part2 = Arduino Uno (Rev3) - ICSP
  S2 = H-Bridge with L298N
  M1 = DC Motor
  Power_12V = Power plug
  M2 = DC Motor
  Part3 = Bluetooth HC-06

nets:
  5V: R1.Pin_0, R2.Pin_0, Part1.5V, Part2.5V, S2.5V, Part3.VCC
  N1: R1.Pin_1, Part1.SDA, Part2.A4/SDA
  N2: R2.Pin_1, Part1.SCL, Part2.A5/SCL
  GND: Part1.GND, Part2.GND, S2.GND, Power_12V.GND, Part3.GND
  N3: Part2.D0/RX, Part3.TXD
  N4: Part2.D1/TX, Part3.RXD
  N5: Part2.D2, S2.IN1
  N6: Part2.D3_PWM, S2.IN2
  N7: Part2.D4, S2.IN3
  N8: Part2.D5_PWM, S2.IN4
  N9: Part2.D6_PWM, S2.ENB
  N10: Part2.D7, S2.ENA
  VIN: Part2.VIN, S2.12V, Power_12V.VCC
  N11: S2.M1-01, M2.pin_2
  N12: S2.M1-02, M2.pin_1
  N13: S2.M2-01, M1.pin_2
  N14: S2.M2-02, M1.pin_1

notes:
  Horizontal Actuator
  Vertical Actuator
  HC-06 Bluetooth
  DS1307 RTC
  L298N Motor Control

custom parts:
  H-Bridge with L298N: h-bridge
